# Fritzing sketch schematic (saved by Fritzing 1.0.1rc)
perfboards: 1
stripboards: 1

parts:
  A1 = Arduino GIGA R1 WiFi
  A2 = Pololu m3s550 motor driver
  A3 = Pololu m3s550 motor driver
  GY1 = GY-521 (MPU-6050) 6pin [form="♀ (female)" package=THT]
  A4 = HC-SR04 Ultrasonic Distance Sensor
  U1 = QTR-9A Reflectance Sensor Array [package=THT]
  DC_Mot_Enc1 = DC Motor with two-phase hall-encoder [part_number=VT-E-G25A-06-177E]
  DC_Mot_Enc2 = DC Motor with two-phase hall-encoder [part_number=VT-E-G25A-06-177E]
  DC_Mot_Enc3 = DC Motor with two-phase hall-encoder [part_number=VT-E-G25A-06-177E]
  DC_Mot_Enc4 = DC Motor with two-phase hall-encoder [part_number=VT-E-G25A-06-177E]
  Part1 = RFID 2 WS1850S
  A5 = HC-SR04 Ultrasonic Distance Sensor
  A6 = HC-SR04 Ultrasonic Distance Sensor
  A7 = HC-SR04 Ultrasonic Distance Sensor
  A8 = HC-SR04 Ultrasonic Distance Sensor
  J1 = Basic Servo
  VCC1 = Battery block 9V  # not connected
  S1 = Pushbutton [package="[THT]"]
  S2 = Pushbutton [package="[THT]"]
  S3 = Pushbutton [package="[THT]"]
  Part3 = I2C level shifter bidirectional
  Part4 = I2C level shifter bidirectional
  Part5 = I2C level shifter bidirectional
  LED1 = RGB LED (com. cathode, rgb) [package="5 mm [THT]"]
  R1 = Resistor [tolerance=±5% resistance=330 package="2010 [SMD]"]
  R2 = Resistor [tolerance=±5% resistance=330 package="2010 [SMD]"]
  J2 = female pin header, 19 pins [form="♀ (female)"]
  J3 = female pin header, 10 pins [form="♀ (female)"]
  J4 = female pin header, 7 pins [form="♀ (female)"]
  J5 = female pin header, 3 pins [form="♀ (female)"]
  J6 = female pin header, 3 pins [form="♀ (female)"]
  J7 = female pin header, 3 pins [form="♀ (female)"]

nets:
  N1: A1.Pin_27, A1.Pin_64, J4.pin1
  N2: A1.Pin_28, A1.Pin_29, A1.Pin_105, A1.Pin_106, A1.Pin_145, A1.Pin_146, J2.pin19, J3.pin1
  N3: A1.Pin_91, Part5.LV1
  N4: A1.Pin_92, Part4.LV3
  N5: A1.Pin_93, Part4.LV1
  N6: A1.Pin_94, Part3.LV3
  N7: A1.Pin_95, Part3.LV1
  N8: A1.Pin_96, A1.Pin_114, U1.9
  N9: A1.Pin_97, U1.7
  N10: A1.Pin_98, U1.5
  N11: A1.Pin_99, U1.3
  N12: A1.Pin_100, U1.1
  N13: A1.Pin_101, DC_Mot_Enc1.pin4
  N14: A1.Pin_102, DC_Mot_Enc3.pin4
  N15: A1.Pin_103, DC_Mot_Enc4.pin4
  N16: A1.Pin_104, DC_Mot_Enc2.pin4
  N17: A1.Pin_109, Part5.LV2
  N18: A1.Pin_110, Part4.LV4
  N19: A1.Pin_111, Part4.LV2
  N20: A1.Pin_112, Part3.LV4
  N21: A1.Pin_113, Part3.LV2
  N22: A1.Pin_115, U1.8
  N23: A1.Pin_116, U1.6
  N24: A1.Pin_117, U1.4
  N25: A1.Pin_118, U1.2
  N26: A1.Pin_119, DC_Mot_Enc1.pin5
  N27: A1.Pin_120, DC_Mot_Enc3.pin5
  N28: A1.Pin_121, DC_Mot_Enc4.pin5
  N29: A1.Pin_122, A1.Pin_139, DC_Mot_Enc2.pin5
  N30: A1.Pin_124, Part1.SCL
  N31: A1.Pin_125, Part1.SDA
  N32: A1.Pin_134, S2.Pin_1, S2.Pin_2, S2.Pin_3, S2.Pin_4, J2.pin4
  N33: A1.Pin_135, S1.Pin_1, S1.Pin_2, S1.Pin_3, S1.Pin_4, J2.pin3
  N34: A1.Pin_136, S3.Pin_1, S3.Pin_2, S3.Pin_3, S3.Pin_4, J2.pin2
  N35: A1.Pin_137, R1.Pin_1
  N36: A1.Pin_138, R2.Pin_1
  N37: A1.Pin_143, A1.Pin_144, J5.pin1
  N38: A1.Pin_147, A1.Pin_148, GY1.pin2
  N39: A1.Pin_149, GY1.pin1
  N40: A2.Pin_27, DC_Mot_Enc3.pin2
  N41: A2.Pin_28, DC_Mot_Enc3.pin1
  N42: A2.Pin_29, J6.pin2
  N43: A2.Pin_30, A2.Pin_41, J7.pin2
  N44: A2.Pin_31, DC_Mot_Enc2.pin2
  N45: A2.Pin_32, DC_Mot_Enc2.pin1
  N46: A3.Pin_16, A3.Pin_29, J6.pin3
  N47: A3.Pin_27, DC_Mot_Enc1.pin2
  N48: A3.Pin_28, DC_Mot_Enc1.pin1
  N49: A3.Pin_30, A3.Pin_53, J7.pin3
  N50: A3.Pin_31, DC_Mot_Enc4.pin2
  N51: A3.Pin_32, DC_Mot_Enc4.pin1
  N52: GY1.pin3, J2.pin18
  N53: GY1.pin5, J3.pin2
  N54: A4.VCC, J3.pin7
  N55: A4.TRIG, Part3.HV1
  N56: A4.ECHO, Part3.HV2
  N57: A4.GND, J2.pin15
  N58: U1.GND, J2.pin16
  N59: U1.VCC, J4.pin2
  N60: U1.CTRL_EVEN, J5.pin2
  N61: U1.CTRL_ODD, J5.pin3
  N62: DC_Mot_Enc1.pin3, J4.pin6
  N63: DC_Mot_Enc1.pin6, J2.pin7
  N64: DC_Mot_Enc2.pin3, J4.pin4
  N65: DC_Mot_Enc2.pin6, J2.pin9
  N66: DC_Mot_Enc3.pin3, J4.pin3
  N67: DC_Mot_Enc3.pin6, J2.pin10
  N68: DC_Mot_Enc4.pin3, J4.pin5
  N69: DC_Mot_Enc4.pin6, J2.pin8
  N70: Part1.5V, J3.pin3
  N71: Part1.GND, J2.pin17
  N72: A5.VCC, J3.pin6
  N73: A5.TRIG, Part4.HV1
  N74: A5.ECHO, Part4.HV2
  N75: A5.GND, J2.pin13
  N76: A6.VCC, J3.pin4
  N77: A6.TRIG, Part5.HV1
  N78: A6.ECHO, Part5.HV2
  N79: A6.GND, J2.pin11
  N80: A7.VCC, J3.pin5
  N81: A7.TRIG, A7.ECHO, Part4.HV3
  N82: A7.GND, J2.pin12
  N83: A8.VCC, J3.pin8
  N84: A8.TRIG, Part3.HV3
  N85: A8.ECHO, Part3.HV4
  N86: A8.GND, J2.pin14
  N87: J1.gnd, J2.pin6
  N88: J1.vcc, J3.pin9
  GND: Part3.GND, Part4.GND, Part5.GND, J2.pin5
  N89: Part3.LV, Part4.LV, Part5.LV, J4.pin7
  N90: Part3.HV, Part4.HV, Part5.HV, J3.pin10
  N91: LED1.red_anode, R1.Pin_0
  N92: LED1.common_cathode, J2.pin1
  N93: LED1.green_anode, R2.Pin_0

custom parts:
  Arduino GIGA R1 WiFi: The Arduino GIGA R1 WiFi is designed for ambitious makers who want to step up their game.
  Pololu m3s550 motor driver: The Motoron M3S550 Triple Motor Controller Shield for Arduino makes it easy to control DC motors from an Arduino or Arduino-compatible board through an I²C interface.
  GY-521 (MPU-6050) 6pin: Placa GY-521 basada en conjunto de acelerómetro+giroscopios MPU-6050
  HC-SR04 Ultrasonic Distance Sensor: The HC-SR04 is an ultrasonic distance sensor. It is capable of providing measurement for ranges of 2cm to 400cm. The module operates at 5V.
  QTR-9A Reflectance Sensor Array: QTR-9A Reflectance Sensor Array (9 analog IR sensors with even/odd LED control).
  RFID 2 WS1850S: An I2C RFID reader module based on the WS1850S (MFRC522-compatible). 4-pin interface: SCL, SDA, 5V, GND.
